# Fritzing sketch projeto (saved by Fritzing 0.9.10b)
breadboards: 2

parts:
  Componente1 = Arduino Uno (Rev3)  # not connected
  Driver2 = 28BYJ-48 Driver Module [part_number=ULN2003 package=THT]
  SM2 = 28BYJ-48 Stepper Motor [part_number=28BYJ-48]
  Power_plug2 = Power plug  # not connected

nets:
  N1: Driver2.blue-pin, SM2.blue-pin
  N2: Driver2.pink-pin, SM2.pink-pin
  N3: Driver2.yellow-pin, SM2.yellow-pin
  N4: Driver2.orange-pin, SM2.orange-pin
  N5: Driver2.red-pin, SM2.red-pin

custom parts:
  28BYJ-48 Driver Module: ULN2003 Driver Module for the 28BYJ-48 Unipolar Stepper Motor LED A - Blue wire - Bottom coil left LED B - Pink wire - Top coil left LED C - Yellow wire - Bottom coil right LED D - Orange wire - Top coil right Common rail - red Connector pins: blue - pink - yellow - orange - red Control pins - IN1 to IN4 Power pins - GND & Vmotor (5-12V) On/Off jumper (if removed, power to motor is cut).
  28BYJ-48 Stepper Motor: Unipolar Stepper Motor 28BYJ-48 Top coil - pink & orange Bottom coil - blue & yellow Common rail - red Connector pins: blue - pink - yellow - orange - red
